# Fritzing sketch schematic_Breathalyser (saved by Fritzing 0.9.3b)
circuit board: 8.46667cm x 5.64444cm
breadboards: 1

parts:
  S1 = Pushbutton [package="[THT]"]
  LED1 = LED - 5mm [color="Red (633nm)" package="5 mm [THT]"]
  Grove1 = Grove OLED 128x96
  Composant3 = Arduino Nano (Rev3.0) (ICSP)
  U1 = Mini-360 DC-DC Buck converter [package=THT]
  U2 = SWITCH_SPDT [package=kps-1290]
  C1 = Electrolytic Capacitor [capacitance=1μF package="0405 [SMD, electrolytic]"]
  R1 = Resistor [tolerance=±5% resistance=220 package=THT]
  BAT1 = Battery Holders [package=battery-aa]
  Composant2 = TP4056 Charger
  MQ-3 = MQ-3 breakout
  J1 = Piezo Speaker
  C2 = Ceramic Capacitor [capacitance=100nF package="200 mil [THT, multilayer]"]
  R2 = Resistor [tolerance=±5% resistance=4.7k package=THT]  # not connected

nets (from the pcb view):
  5V: S1.Pin_1, S1.Pin_2, Composant3.5V, MQ-3.VCC, C2.1
  N1: S1.Pin_3, S1.Pin_4, Composant3.D3, C2.0
  GND: LED1.cathode, Grove1.GND, Composant3.GND, U1.IN-, U1.OUT-, U2.S, C1.-, BAT1.-, Composant2.IN-, Composant2.BAT-, MQ-3.GND, J1.pin1
  N2: LED1.anode, R1.Pin_1
  VCC: Grove1.VCC, Composant3.3V3
  N3: Grove1.SDA, Composant3.A4
  N4: Grove1.SCL, Composant3.A5
  N5: Composant3.D2, R1.Pin_0
  N6: Composant3.D4, J1.pin2
  N7: Composant3.VIN, U1.OUT+, C1.+
  N8: Composant3.A7, MQ-3.AO
  N9: U1.IN+, U2.P
  N10: U2.O, BAT1.+, Composant2.BAT+

custom parts:
  Mini-360 DC-DC Buck converter: Mini-360 DC-DC Buck converter. Tiny buck step down voltage converter, input voltage 4.75 to 23V output 1 to 17V adjustable. Available from ebay and the like.
  MQ-3 breakout: Alcohol sensor is capable of detecting alcohol (ethanol) particles on itself and gives the information in digital form back to us to manipulate with it. SKU:101251 • Voltage: 5V DC • Power: max 750mW • Measurement range: 0.04-4mg/L
